// Digital circuit 1-bit-flip-flop.dig as structural Verilog
module _1_bit_flip_flop (
  input  D,
  input  EN,
  input  CLK,
  input  CLR
);

  wire d_latch_clr_1_q, d_latch_clr_2_q, multiplexer_1_out, not_1_out;

  Multiplexer multiplexer_1 (.sel(EN), .in_0(d_latch_clr_2_q), .in_1(D), .out(multiplexer_1_out));
  not not_1 (not_1_out, CLK);
  d_latch_clr d_latch_clr_1 (.CLK(not_1_out), .D(multiplexer_1_out), .CLR(CLR), .Q(d_latch_clr_1_q));  // open: notQ
  d_latch_clr d_latch_clr_2 (.CLK(CLK), .D(d_latch_clr_1_q), .CLR(CLR), .Q(d_latch_clr_2_q));  // open: notQ
endmodule
