// Digital circuit 3_27_sketch.dig as structural Verilog
module _3_27_sketch (
  input  [7:0] a,
  input  [7:0] b,
  input  sel,
  input  [1:0] sel_2,
  input  in_10,
  input  in_11,
  input  in_12,
  input  in_13,
  input  [7:0] addr,
  output [7:0] out_3,
  output out_5,
  output out_6,
  output out_7,
  output out_8,
  output [1:0] out_14,
  output [31:0] iw
);

  Multiplexer #(.Bits(8)) multiplexer_1 (.sel(sel), .in_0(a), .in_1(b), .out(out_3));
  Decoder #(.Selector_Bits(2)) decoder_1 (.sel(sel_2), .out_0(out_5), .out_1(out_6), .out_2(out_7), .out_3(out_8));
  ROM #(.AddrBits(8), .Bits(32)) rom_1 (.A(addr), .sel(1'b1), .D(iw));
  PriorityEncoder #(.Selector_Bits(2)) priorityencoder_1 (
    .in0(in_10), .in1(in_11), .in2(in_12), .in3(in_13), .num(out_14));  // open: any

  // Notes on the sheet:
  //   contents of rom_1 (hex, n*v repeats v):
  //   100293,a2c463,8067,fe810113,113023,a13423,fff50513,fe5ff0ef,a13823
  //   ,813503,ffe50513,fd5ff0ef,1013303,650533,13083,1810113,8067,c0001073
endmodule
