// Digital circuit 3_27_sketch.dig as structural Verilog
module _3_27_sketch (
  input  [3:0] in_1,
  input  [3:0] in_2,
  input  [3:0] in_3,
  input  [3:0] in_4,
  input  [1:0] sel,
  input  [1:0] sel_2,
  input  in_12,
  input  in_13,
  input  in_14,
  input  in_15,
  input  [7:0] in_17,
  output [3:0] out_6,
  output out_8,
  output out_9,
  output out_10,
  output out_11,
  output [1:0] out_16,
  output [31:0] out_18
);

  Multiplexer #(.Bits(4), .Selector_Bits(2)) multiplexer_1 (
    .sel(sel), .in_0(in_1), .in_1(in_2), .in_2(in_3), .in_3(in_4), .out(out_6));
  ROM #(.AddrBits(8), .Bits(32)) rom_1 (.A(in_17), .sel(1'b1), .D(out_18));
  Decoder #(.Selector_Bits(2)) decoder_1 (.sel(sel_2), .out_0(out_8), .out_1(out_9), .out_2(out_10), .out_3(out_11));
  PriorityEncoder #(.Selector_Bits(2)) priorityencoder_1 (
    .in0(in_12), .in1(in_13), .in2(in_14), .in3(in_15), .num(out_16));  // open: any

  // Other names for the same wires on the sheet: IW[31:0] = out_18

  // Notes on the sheet:
  //   contents of rom_1 (hex, n*v repeats v):
  //   c5c663,100513,3c0006f,b502b3,28283,c50333,30303,628663,513,200006f
  //   ,ff810113,113023,158593,fff60613,fc9ff0ef,13083,810113,8067,c0001073
endmodule
