// Digital circuit d-latch-clr.dig as structural Verilog
module d_latch_clr (
  input  CLK,
  input  D,
  input  CLR,
  output Q,
  output notQ
);

  wire and_1_out, or_1_out;

  or or_1 (or_1_out, CLK, CLR);
  and and_1 (and_1_out, D, ~CLR);  // And
  // d_latch d_latch_1: pin names not known; wires that end beside it: or_1_out, and_1_out, Q, notQ
endmodule
